// Logisim project ALU Control.circ as structural Verilog
module ALU_Control (
  input  [1:0] ALU_OP,
  input  [3:0] Funct_Bits,
  output [3:0] ALU_Control_Op
);

  wire and_2_out, not_1_out, not_2_out;

  not not_1 (not_1_out, ALU_OP[1]);
  not not_2 (not_2_out, Funct_Bits[2]);
  and and_1 (ALU_Control_Op[0], ALU_OP[1], Funct_Bits[0]);
  or or_1 (ALU_Control_Op[1], not_1_out, not_2_out);
  and and_2 (and_2_out, ALU_OP[1], Funct_Bits[1]);
  or or_2 (ALU_Control_Op[2], ALU_OP[0], and_2_out);

  assign ALU_Control_Op[3] = 1'b0;
endmodule
