// Logisim project Control Unit.circ as structural Verilog
module Control_Unit (
  input  a,
  input  b,
  input  c,
  output RegDest,
  output RegWrite,
  output MemRead,
  output MemWrite,
  output MemToReg,
  output Branch,
  output Jump,
  output ALUSRC,
  output ALUOP1,
  output ALUOP2
);

  wire and_1_out, and_2_out, and_3_out, and_4_out, and_5_out, and_6_out, and_7_out, and_8_out, and_9_out,
       and_13_out, and_14_out, and_15_out, not_1_out, not_2_out, not_3_out, not_4_out, not_5_out, not_6_out,
       not_7_out, not_8_out, not_9_out, not_10_out, not_11_out, not_12_out, not_13_out, not_14_out,
       not_15_out, not_16_out, not_17_out, not_18_out, not_19_out, not_20_out, not_21_out, not_22_out,
       not_23_out, not_24_out, not_25_out, not_26_out, not_27_out;

  not not_1 (not_1_out, a);
  not not_2 (not_2_out, b);
  not not_3 (not_3_out, a);
  not not_4 (not_4_out, c);
  not not_5 (not_5_out, b);
  not not_6 (not_6_out, c);
  not not_7 (not_7_out, a);
  not not_8 (not_8_out, b);
  not not_9 (not_9_out, a);
  not not_10 (not_10_out, c);
  not not_11 (not_11_out, b);
  not not_12 (not_12_out, c);
  not not_13 (not_13_out, a);
  not not_14 (not_14_out, b);
  not not_15 (not_15_out, a);
  not not_16 (not_16_out, c);
  not not_17 (not_17_out, a);
  not not_18 (not_18_out, b);
  not not_19 (not_19_out, a);
  not not_20 (not_20_out, c);
  not not_21 (not_21_out, a);
  not not_22 (not_22_out, b);
  not not_23 (not_23_out, a);
  not not_24 (not_24_out, c);
  not not_25 (not_25_out, b);
  not not_26 (not_26_out, c);
  not not_27 (not_27_out, a);
  and and_1 (and_1_out, not_1_out, not_2_out);
  and and_2 (and_2_out, not_3_out, not_4_out);
  and and_3 (and_3_out, not_5_out, not_6_out);
  and and_4 (and_4_out, not_7_out, not_8_out);
  and and_5 (and_5_out, not_9_out, not_10_out);
  and and_6 (and_6_out, not_11_out, not_12_out);
  and and_7 (and_7_out, a, b, c);
  and and_8 (and_8_out, not_13_out, not_14_out);
  and and_9 (and_9_out, not_15_out, not_16_out);
  and and_10 (MemToReg, not_17_out, not_18_out, c);
  and and_11 (Branch, not_19_out, b, c);
  and and_12 (Jump, a, b, not_20_out);
  and and_13 (and_13_out, not_21_out, not_22_out);
  and and_14 (and_14_out, not_23_out, not_24_out);
  and and_15 (and_15_out, not_25_out, not_26_out);
  and and_16 (ALUOP2, not_27_out, c);
  or or_1 (RegDest, and_1_out, and_2_out, and_3_out);
  or or_2 (RegWrite, and_4_out, and_5_out, and_6_out, and_7_out);
  or or_3 (MemRead, and_8_out, and_9_out);
  or or_4 (ALUSRC, and_13_out, and_14_out, and_15_out);

  assign ALUOP1 = 1'b0;
  assign MemWrite = 1'b0;
endmodule
