// Logisim project Final.circ as structural Verilog: 1 circuit, main circuit main
module main (
  input  in_1,
  input  in_2,
  output [15:0] out_3,
  output [15:0] out_4,
  output [15:0] out_5,
  output [15:0] out_6,
  output [15:0] out_7,
  output [15:0] out_8,
  output out_9,
  output [1:0] out_10,
  output [3:0] out_11
);

  wire AluSrc, and_1_out, Branch, jump, MemRead, MemToReg, MemWrite, RegDst, RegWrite;
  wire [1:0] Control_Unit_aluop1;
  wire [2:0] multiplexer_1_out;
  wire [15:0] adder_1_out, bit_extender_1_out, Jump_p3, multiplexer_2_out, multiplexer_3_out,
       multiplexer_4_out, n16_bit_alu_1_p6, n16_bit_register_file_1_read_data_1, PC_q, ram_1_data, rom_1_data;

  Register #(.width(16)) PC (.D(multiplexer_4_out), .Q(PC_q), .clk(in_2), .clr(1'b0));  // open: en
  Adder #(.width(16)) adder_1 (.a(PC_q), .b(16'h1), .out(adder_1_out), .cin(in_1));  // open: cout
  ROM #(.addrWidth(16), .dataWidth(16)) rom_1 (.addr(PC_q), .data(rom_1_data));  // open: sel
  Control_Unit Control_Unit (
    .a(rom_1_data[15]), .b(rom_1_data[14]), .c(rom_1_data[13]), .RegDest(RegDst), .RegWrite(RegWrite),
    .MemRead(MemRead), .MemWrite(MemWrite), .MemToReg(MemToReg), .Branch(Branch), .Jump(jump),
    .ALUSRC(AluSrc), .ALUOP1(Control_Unit_aluop1[0]), .ALUOP2(Control_Unit_aluop1[1]));
  // Jump Jump: pin names not known; wires that end beside it: adder_1_out, rom_1_data, Jump_p3
  Multiplexer #(.width(3), .enable("false")) multiplexer_1 (
    .in0(rom_1_data[9:7]), .in1(rom_1_data[6:4]), .out(multiplexer_1_out), .sel(RegDst));
  _16_Bit_Register_File u_16_bit_register_file_1 (
    .Write_Data(out_4), .Read_Data_1(n16_bit_register_file_1_read_data_1),
    .Read_Register_1(rom_1_data[12:10]), .Read_Data_2(out_7), .Read_Register_2(rom_1_data[9:7]),
    .RegWrite(RegWrite), .CLK(in_2), .Write_Register(multiplexer_1_out), .out_7(out_8), .out_8(out_5),
    .out_9(out_3), .out_10(out_6));
  assign bit_extender_1_out = {{12{rom_1_data[3]}}, rom_1_data[3:0]};  // Bit_Extender bit_extender_1
  Multiplexer #(.width(16), .enable("false")) multiplexer_2 (
    .in0(out_7), .in1(bit_extender_1_out), .out(multiplexer_2_out), .sel(AluSrc));
  Multiplexer #(.width(16), .enable("false")) multiplexer_3 (
    .in0(adder_1_out), .in1(bit_extender_1_out), .out(multiplexer_3_out), .sel(and_1_out));
  and and_1 (and_1_out, Branch, out_9);
  ALU_Control ALU_OP (
    .ALU_OP(Control_Unit_aluop1), .Funct_Bits(rom_1_data[3:0]), .ALU_Control_Op({out_11[3:2], out_10}));
  // _16_Bit_ALU 16_bit_alu_1: pin names not known; wires that end beside it: n16_bit_register_file_1_read_data_1, multiplexer_2_out, out_11[2], out_10, out_9, n16_bit_alu_1_p6
  Multiplexer #(.width(16), .enable("false")) multiplexer_4 (
    .in0(multiplexer_3_out), .in1(Jump_p3), .out(multiplexer_4_out), .sel(jump));
  Multiplexer #(.width(16), .enable("false")) multiplexer_5 (
    .in0(n16_bit_alu_1_p6), .in1(ram_1_data), .out(out_4), .sel(MemToReg));
  RAM #(.addrWidth(16), .dataWidth(16), .bus("separate")) ram_1 (
    .addr(n16_bit_alu_1_p6), .din(out_7), .data(ram_1_data), .str(MemWrite), .clk(in_2), .ld(MemRead));  // open: sel, clr

  assign out_11[1:0] = out_10;

  // Notes on the sheet:
  //   OpCode
  //   contents of rom_1 (hex, n*v repeats v):
  //   11 2020 24b0 482f 6808 4491 24c0 6e83 9030 65519*0 9030
endmodule
